// Logisim project a1-g6-circuit.circ as structural Verilog: 1 circuit, main circuit X0
module X0 (
  input  A3,
  input  B3,
  input  A2,
  input  B2,
  input  A1,
  input  B1,
  input  A0,
  input  B0,
  input  CS2,
  input  CS0,
  input  CS1
);

  wire adder_1_cout, adder_1_out, adder_2_cout, adder_2_out, adder_3_cout, adder_3_out, adder_4_cout,
       adder_4_out, and_1_out, and_2_out, and_3_out, and_4_out, and_5_out, and_6_out, and_7_out, and_8_out,
       and_9_out, and_10_out, and_11_out, and_12_out, and_13_out, and_14_out, and_15_out, and_16_out,
       nor_1_out, nor_2_out, nor_3_out, not_1_out, not_2_out, not_3_out, not_4_out, not_5_out, not_6_out,
       or_1_out, or_2_out, or_3_out, or_4_out, or_5_out, or_6_out, or_7_out, or_8_out, or_9_out, or_10_out,
       or_11_out;

  not not_1 (not_1_out, B3);
  not not_2 (not_2_out, B2);
  not not_3 (not_3_out, B1);
  not not_4 (not_4_out, B0);
  and and_1 (and_1_out, CS0, not_1_out);
  and and_2 (and_2_out, CS0, not_2_out);
  and and_3 (and_3_out, CS0, not_3_out);
  and and_4 (and_4_out, CS0, not_4_out);
  not not_5 (not_5_out, CS0);
  not not_6 (not_6_out, CS1);
  and and_5 (and_5_out, and_1_out, not_6_out);
  and and_6 (and_6_out, and_2_out, not_6_out);
  and and_7 (and_7_out, and_3_out, not_6_out);
  and and_8 (and_8_out, and_4_out, not_6_out);
  or or_1 (or_1_out, and_5_out, A3);
  or or_2 (or_2_out, and_6_out, A2);
  or or_3 (or_3_out, and_7_out, A1);
  or or_4 (or_4_out, and_8_out, A0);
  or or_5 (or_5_out, CS1, not_1_out);
  or or_6 (or_6_out, CS1, not_2_out);
  or or_7 (or_7_out, CS1, not_3_out);
  or or_8 (or_8_out, CS1, not_4_out);
  and and_9 (and_9_out, not_5_out, adder_2_cout);
  and and_10 (and_10_out, not_5_out, adder_3_cout);
  and and_11 (and_11_out, not_5_out, adder_4_cout);
  and and_12 (and_12_out, not_5_out, CS2);
  Adder #(.width(1)) adder_1 (.a(or_1_out), .b(or_5_out), .out(adder_1_out), .cin(and_9_out), .cout(adder_1_cout));
  Adder #(.width(1)) adder_2 (.a(or_2_out), .b(or_6_out), .out(adder_2_out), .cin(and_10_out), .cout(adder_2_cout));
  Adder #(.width(1)) adder_3 (.a(or_3_out), .b(or_7_out), .out(adder_3_out), .cin(and_11_out), .cout(adder_3_cout));
  Adder #(.width(1)) adder_4 (.a(or_4_out), .b(or_8_out), .out(adder_4_out), .cin(and_12_out), .cout(adder_4_cout));
  and and_13 (and_13_out, not_5_out, adder_1_cout);
  LED F3 (.in(adder_1_out));
  LED F2 (.in(adder_2_out));
  LED F1 (.in(adder_3_out));
  LED F0 (.in(adder_4_out));
  or or_9 (or_9_out, adder_4_out, adder_3_out);
  or or_10 (or_10_out, adder_2_out, adder_1_out);
  and and_14 (and_14_out, not_5_out, adder_1_out);
  nor nor_1 (nor_1_out, and_9_out, and_9_out);
  and and_15 (and_15_out, nor_1_out, and_13_out);
  nor nor_2 (nor_2_out, and_13_out, and_13_out);
  and and_16 (and_16_out, and_9_out, nor_2_out);
  nor nor_3 (nor_3_out, or_9_out, or_10_out);
  or or_11 (or_11_out, and_16_out, and_15_out);
  LED CF (.in(and_13_out));
  LED ZF (.in(nor_3_out));
  LED SF (.in(and_14_out));
  LED VF (.in(or_11_out));

  // Notes on the sheet:
  //   B3'
  //   B2'
  //   B1'
  //   B0'
  //   Y3
  //   Y2
  //   Y1
  //   Y0
  //   X3
  //   C3.CS0'
  //   X2
  //   C2.CS0'
  //   X1
  //   C1.CS0'
  //   X0
  //   C0/Cin
  //   C4
  //   C3
  //   C2
  //   C1
  //   C4.CS0'
  //   CS0'
  //   C3.CS0'
endmodule
