// Logisim project A1_6.circ as structural Verilog: 9 circuits, main circuit main
module main (
  input  Reset_PC,
  output out_2,
  output [7:0] Read_Data_1,
  output [7:0] A,
  output [7:0] B,
  output [7:0] new_PC,
  output [7:0] Read_Data_2,
  output [7:0] F,
  output [7:0] write_data,
  output [7:0] Read_Data,
  output [3:0] Opcode,
  output [2:0] ALUop
);

  wire alu_1_zf, and_1_out, and_2_out, and_3_out, clock_1_out, control_unit_1_alusrc1,
       control_unit_1_branch_equal, control_unit_1_branch_not_equal, control_unit_1_jump,
       control_unit_1_memread, control_unit_1_memtoreg, control_unit_1_memwrite, control_unit_1_regdst,
       control_unit_1_regwrite, not_1_out, registers_1_is_sp;
  wire [1:0] control_unit_1_alusrc2, priority_encoder_1_out;
  wire [3:0] multiplexer_1_out;
  wire [7:0] adder_1_out, multiplexer_5_out, PC_q;
  wire [15:0] rom_1_data;

  Register #(.trigger("falling")) PC (.D(new_PC), .Q(PC_q), .clk(clock_1_out), .clr(Reset_PC));  // open: en
  Clock clock_1 (.out(clock_1_out));
  Adder adder_1 (.a(PC_q), .b(8'h1), .out(adder_1_out), .cin(1'b0), .cout(out_2));
  ROM #(.dataWidth(20)) rom_1 (.addr(PC_q), .data({Opcode, rom_1_data}));  // open: sel
  Multiplexer #(.width(4), .enable("false")) multiplexer_1 (
    .in0(rom_1_data[11:8]), .in1(rom_1_data[7:4]), .out(multiplexer_1_out), .sel(control_unit_1_regdst));
  Control_Unit control_unit_1 (
    .Opcode(Opcode), .RegWrite(control_unit_1_regwrite), .MemRead(control_unit_1_memread),
    .MemWrite(control_unit_1_memwrite), .MemtoReg(control_unit_1_memtoreg), .RegDst(control_unit_1_regdst),
    .ALUSrc1(control_unit_1_alusrc1), .ALUSrc2(control_unit_1_alusrc2), .ALUop(ALUop),
    .branch_equal(control_unit_1_branch_equal), .branch_not_equal(control_unit_1_branch_not_equal),
    .jump(control_unit_1_jump));
  Registers registers_1 (
    .WriteData(write_data), .ReadRegister1(rom_1_data[15:12]), .RegWrite(control_unit_1_regwrite),
    .WriteRegister(multiplexer_1_out), .ReadRegister2(rom_1_data[11:8]), .ReadData1(Read_Data_1),
    .is_sp(registers_1_is_sp), .ReadData2(Read_Data_2));
  Multiplexer #(.width(8), .enable("false")) multiplexer_2 (
    .in0(Read_Data_1), .in1(Read_Data_2), .out(A), .sel(control_unit_1_alusrc1));
  Multiplexer #(.select(2), .width(8), .enable("false")) multiplexer_3 (
    .in0(Read_Data_2), .in1({4'b0000, rom_1_data[3:0]}), .in2(rom_1_data[7:0]), .in3({8{1'b0}}), .out(B),
    .sel(control_unit_1_alusrc2));
  Multiplexer #(.width(8), .enable("false")) multiplexer_4 (
    .in0(F), .in1(Read_Data), .out(write_data), .sel(control_unit_1_memtoreg));
  ALU alu_1 (.A(A), .B(B), .ALUop(ALUop), .ZF(alu_1_zf), .F(F));  // open: out_4, out_5
  and and_1 (and_1_out, control_unit_1_branch_equal, alu_1_zf);
  not not_1 (not_1_out, alu_1_zf);
  and and_2 (and_2_out, not_1_out, control_unit_1_branch_not_equal);
  Multiplexer #(.select(2), .width(8), .enable("false")) multiplexer_5 (
    .in0(adder_1_out), .in1(rom_1_data[7:0]), .in2(rom_1_data[7:0]), .in3(rom_1_data[15:8]),
    .out(multiplexer_5_out), .sel(priority_encoder_1_out));
  DataMemory datamemory_1 (
    .Address(F), .WriteData(Read_Data_2), .MemWrite(control_unit_1_memwrite),
    .MemRead(control_unit_1_memread), .is_sp(registers_1_is_sp), .ReadData(Read_Data));
  Priority_Encoder #(.select(2)) priority_encoder_1 (
    .in0(1'b1), .in1(and_1_out), .in2(and_2_out), .in3(control_unit_1_jump), .out(priority_encoder_1_out));  // open: gs, en_out, en_in
  and and_3 (and_3_out, control_unit_1_jump, rom_1_data[0]);
  Multiplexer #(.width(8), .enable("false")) multiplexer_6 (
    .in0(multiplexer_5_out), .in1(Read_Data_1), .out(new_PC), .sel(and_3_out));

  // Notes on the sheet:
  //   Instruction Memory
  //   contents of rom_1 (hex, n*v repeats v):
  //   c06ff 70000 f0600 71104 72205 e1230 7330e
  //   Registers
  //   ALU
  //   Data Memory Unit
endmodule

module ALU (
  input  [7:0] A,
  input  [7:0] B,
  input  [2:0] ALUop,
  output out_4,
  output out_5,
  output ZF,
  output [7:0] F
);

  wire [7:0] adder_1_out, and_1_out, nor_1_out, or_1_out, subtractor_1_out;
  wire [15:0] shifter_1_out, shifter_2_out;

  Adder adder_1 (.a(A), .b(B), .out(adder_1_out), .cin(1'b0), .cout(out_4));
  Subtractor subtractor_1 (.a(A), .b(B), .out(subtractor_1_out), .bin(1'b0), .bout(out_5));
  assign or_1_out = A | B;  // OR_Gate or_1, 8 bits wide
  assign and_1_out = A & B;  // AND_Gate and_1, 8 bits wide
  assign nor_1_out = ~(A | B);  // NOR_Gate nor_1, 8 bits wide
  Shifter #(.width(16)) shifter_1 (.in({{8{1'b0}}, A}), .\dist (B[3:0]), .out(shifter_1_out));
  Shifter #(.width(16), .shift("lr")) shifter_2 (.in({{8{1'b0}}, A}), .\dist (B[3:0]), .out(shifter_2_out));
  Multiplexer #(.select(3), .width(8), .enable("false")) multiplexer_1 (
    .in0(adder_1_out), .in1(subtractor_1_out), .in2(or_1_out), .in3(and_1_out), .in4(nor_1_out),
    .in5(shifter_1_out[7:0]), .in6(shifter_2_out[7:0]), .in7({8{1'b0}}), .out(F), .sel(ALUop));
  nor nor_2 (ZF, F[0], F[1], F[2], F[3], F[4], F[5], F[6], F[7]);
endmodule

module Registers (
  input  [7:0] WriteData,
  input  [3:0] ReadRegister1,
  input  RegWrite,
  input  [3:0] WriteRegister,
  input  [3:0] ReadRegister2,
  output [7:0] ReadData1,
  output is_sp,
  output [7:0] ReadData2
);

  wire clock_1_out, decoder_1_out0, decoder_1_out1, decoder_1_out2, decoder_1_out3, decoder_1_out4,
       decoder_1_out5, decoder_1_out6, decoder_1_out7, not_1_out;
  wire [7:0] sp_q, t0_q, t1_q, t2_q, t3_q, t4_q, zero_q;

  Decoder #(.select(3), .disabled(0)) decoder_1 (
    .out0(decoder_1_out0), .out1(decoder_1_out1), .out2(decoder_1_out2), .out3(decoder_1_out3),
    .out4(decoder_1_out4), .out5(decoder_1_out5), .out6(decoder_1_out6), .out7(decoder_1_out7),
    .sel(WriteRegister[2:0]), .en(RegWrite));
  Clock clock_1 (.out(clock_1_out));
  Register #(.trigger("falling")) zero (
    .D(WriteData), .en(decoder_1_out0), .Q(zero_q), .clk(clock_1_out));  // open: clr
  Register #(.trigger("falling")) t0 (.D(WriteData), .en(decoder_1_out1), .Q(t0_q), .clk(clock_1_out));  // open: clr
  Register #(.trigger("falling")) t1 (.D(WriteData), .en(decoder_1_out2), .Q(t1_q), .clk(clock_1_out));  // open: clr
  Register #(.trigger("falling")) t2 (.D(WriteData), .en(decoder_1_out3), .Q(t2_q), .clk(clock_1_out));  // open: clr
  Register #(.trigger("falling")) t3 (.D(WriteData), .en(decoder_1_out4), .Q(t3_q), .clk(clock_1_out));  // open: clr
  Register #(.trigger("falling")) t4 (.D(WriteData), .en(decoder_1_out5), .Q(t4_q), .clk(clock_1_out));  // open: clr
  Register #(.trigger("falling")) sp (.D(WriteData), .en(decoder_1_out6), .Q(sp_q), .clk(clock_1_out));  // open: clr
  Multiplexer #(.select(3), .width(8), .enable("false")) multiplexer_1 (
    .in0(zero_q), .in1(t0_q), .in2(t1_q), .in3(t2_q), .in4(t3_q), .in5(t4_q), .in6(sp_q), .in7({8{1'b0}}),
    .out(ReadData1), .sel(ReadRegister1[2:0]));
  Multiplexer #(.select(3), .width(8), .enable("false")) multiplexer_2 (
    .in0(zero_q), .in1(t0_q), .in2(t1_q), .in3(t2_q), .in4(t3_q), .in5(t4_q), .in6(sp_q), .in7({8{1'b0}}),
    .out(ReadData2), .sel(ReadRegister2[2:0]));
  not not_1 (not_1_out, ReadRegister1[0]);
  and and_1 (is_sp, not_1_out, ReadRegister1[1], ReadRegister1[2]);
endmodule

module DataMemory (
  input  [7:0] Address,
  input  [7:0] WriteData,
  input  MemWrite,
  input  MemRead,
  input  is_sp,
  output [7:0] ReadData
);

  wire clock_1_out, not_1_out;
  wire [7:0] ram_1_data, ram_2_data;

  Clock clock_1 (.out(clock_1_out));
  not not_1 (not_1_out, is_sp);
  RAM #(.bus("separate")) ram_1 (
    .addr(Address), .din(WriteData), .data(ram_1_data), .str(MemWrite), .sel(not_1_out), .clk(clock_1_out),
    .ld(MemRead));  // open: clr
  RAM #(.bus("separate")) ram_2 (
    .addr(Address), .din(WriteData), .data(ram_2_data), .str(MemWrite), .sel(is_sp), .clk(clock_1_out),
    .ld(MemRead));  // open: clr
  Multiplexer #(.width(8), .enable("false")) multiplexer_1 (
    .in0(ram_1_data), .in1(ram_2_data), .out(ReadData), .sel(is_sp));

  // Notes on the sheet:
  //   Data Memory
  //   Stack Memory
endmodule

module ControlUnit (
  input  [3:0] Opcode,
  output RegWrite,
  output MemRead,
  output MemWrite,
  output MemtoReg,
  output RegDst,
  output ALUSrc1,
  output [1:0] ALUSrc2,
  output [2:0] ALUop,
  output branch_equal,
  output branch_not_equal,
  output jump
);

  wire or_1_out, or_2_out, or_3_out, or_4_out;
  wire [1:0] decoder_1_out1, decoder_1_out7;
  wire [6:0] decoder_1_out3;

  Decoder #(.select(4), .enable("false")) decoder_1 (
    .out0(decoder_1_out3[5]), .out1(decoder_1_out1[0]), .out2(decoder_1_out1[1]), .out3(decoder_1_out3[0]),
    .out4(decoder_1_out3[6]), .out5(MemRead), .out6(MemWrite), .out7(decoder_1_out7[0]),
    .out8(branch_not_equal), .out9(decoder_1_out3[1]), .out10(branch_equal), .out11(decoder_1_out3[2]),
    .out12(decoder_1_out7[1]), .out13(decoder_1_out3[3]), .out14(decoder_1_out3[4]), .out15(jump),
    .sel(Opcode));
  or or_1 (or_1_out, MemWrite, MemRead, decoder_1_out7[1], decoder_1_out3[4]);
  or or_2 (or_2_out, decoder_1_out1[0], branch_not_equal, branch_equal, decoder_1_out3[2]);
  or or_3 (or_3_out, decoder_1_out3[0], decoder_1_out7[0]);
  or or_4 (or_4_out, decoder_1_out1[1], decoder_1_out3[3]);
  or or_5 (ALUSrc2[1], decoder_1_out1[0], decoder_1_out1[1], MemRead, MemWrite, decoder_1_out7[0], decoder_1_out7[1]);
  Priority_Encoder priority_encoder_1 (
    .in0(or_1_out), .in1(or_2_out), .in2(or_3_out), .in3(or_4_out), .in4(decoder_1_out3[1]),
    .in5(decoder_1_out3[5]), .in6(decoder_1_out3[6]), .in7(jump), .out(ALUop));  // open: en_in, gs, en_out
  or or_6 (RegWrite, decoder_1_out3[0], decoder_1_out3[1], decoder_1_out3[2], decoder_1_out3[3], decoder_1_out3[4], decoder_1_out1[0], decoder_1_out1[1], MemRead, decoder_1_out7[0], decoder_1_out7[1], decoder_1_out3[5], decoder_1_out3[6]);
  or or_7 (RegDst, decoder_1_out3[0], decoder_1_out3[1], decoder_1_out3[2], decoder_1_out3[3], decoder_1_out3[4], decoder_1_out3[5], decoder_1_out3[6]);
  or or_8 (ALUSrc1, decoder_1_out3[5], decoder_1_out3[6]);

  assign ALUSrc2[0] = ALUSrc1;
  assign MemtoReg = MemRead;

  // Notes on the sheet:
  //   Shifts
  //   R-type (except shifts)
  //   I-type (except branch)
endmodule

module test_reg (
  input  [7:0] in_1,
  input  [3:0] in_2,
  input  [3:0] in_3,
  input  [3:0] in_4,
  input  in_5,
  output [7:0] out_6,
  output [7:0] out_7,
  output out_8
);

  Registers registers_1 (
    .WriteData(in_1), .ReadRegister1(in_2), .RegWrite(in_5), .WriteRegister(in_3), .ReadRegister2(in_4),
    .ReadData1(out_6), .is_sp(out_8), .ReadData2(out_7));
endmodule

module test_mem (
  input  [7:0] in_1,
  input  [7:0] in_2,
  input  in_3,
  input  in_4,
  input  in_5,
  output [7:0] out_6
);

  DataMemory datamemory_1 (
    .Address(in_1), .WriteData(in_2), .MemWrite(in_3), .MemRead(in_4), .is_sp(in_5), .ReadData(out_6));
endmodule

module Control_Unit (
  input  [3:0] Opcode,
  output RegWrite,
  output MemRead,
  output MemWrite,
  output MemtoReg,
  output RegDst,
  output ALUSrc1,
  output [1:0] ALUSrc2,
  output [2:0] ALUop,
  output branch_equal,
  output branch_not_equal,
  output jump
);

  wire [15:14] rom_1_data;

  ROM #(.addrWidth(4), .dataWidth(16)) rom_1 (
    .addr(Opcode),
    .data({rom_1_data, jump, branch_not_equal, branch_equal, ALUop, ALUSrc2, ALUSrc1, RegDst, MemtoReg, MemWrite, MemRead, RegWrite}));  // open: sel

  // Notes on the sheet:
  //   contents of rom_1 (hex, n*v repeats v):
  //   571 181 381 211 671 8b 84 281 1100 411 900 111 81 311 11 2700
endmodule

module sample (
  input  a,
  input  b,
  output c
);


  assign c = b;
endmodule
